# Fritzing sketch schematic (saved by Fritzing 0.9.3b)
circuit board: 5.25286cm x 5.26388cm

parts:
  Q1 = NPN-Transistor [package="SOT-23 [SMD]"]
  U1 = ESP8266 WiFi Module [part_number=ESP8266]
  STM32_EVB = BluePill
  R1 = Resistor [tolerance=±5% resistance=10k package="0805 [SMD]"]
  R2 = Resistor [tolerance=±5% resistance=10k package="0805 [SMD]"]
  R3 = Resistor [tolerance=±5% resistance=10k package="0805 [SMD]"]
  R4 = Resistor [tolerance=±5% resistance=10k package="0805 [SMD]"]
  R5 = Resistor [tolerance=±5% resistance=10k package="0805 [SMD]"]
  R6 = Resistor [tolerance=±5% resistance=2k package="0805 [SMD]"]
  LED_strip = ws2812b [package=THT]
  PIR_sensor = HC-SR501 Body Sensor Module

nets:
  GND: Q1.2, U1.GND, STM32_EVB.GND2, LED_strip.VSS, PIR_sensor.GND
  N1: Q1.0, R1.Pin_1
  STM32_BOOT0: Q1.1, R2.Pin_0
  N2: U1.RXD, STM32_EVB.A9
  3.3V: U1.VCC, STM32_EVB.3V3, R2.Pin_1, R3.Pin_1, R4.Pin_1, R5.Pin_1
  N3: U1.GPIO_0, R5.Pin_0, R6.Pin_0
  N4: U1.GPIO_2, R1.Pin_0, R3.Pin_0
  N5: U1.CH_PD, R4.Pin_0
  N6: U1.TXD, STM32_EVB.A10
  STM32_NRST: STM32_EVB.NRST, R6.Pin_1
  5V: STM32_EVB.5V, LED_strip.VDD, PIR_sensor.VCC
  N7: STM32_EVB.B12, LED_strip.DIN
  N8: STM32_EVB.B1, PIR_sensor.OUT

notes:
  STM32 BOOT0

custom parts:
  ESP8266 WiFi Module: Generic WiFi Module based on the ESP8266 with onboard PCB antenna and UART communications
  HC-SR501 Body Sensor Module: Pyroelectric Infrared PIR Motion Sensor Detector Module
